# Fritzing sketch Lock (saved by Fritzing 0.9.10b)
breadboards: 1

parts:
  LED1 = LED - 3mm [color="Red (633nm)" current=0.030 package="3 mm [THT]"]
  LED3 = LED - 3mm [color="Blue (470nm)" current=0.030 package="3 mm [THT]"]
  U1 = ESP8266 WiFi Module [part_number=ESP8266]
  LED6 = LED - 3mm [color="Green (560nm)" current=0.030 package="3 mm [THT]"]
  Arduino_Uno = Arduino Uno (Rev3)
  M1 = Grove Electromagnet
  IR_Receiver1 = IR_Receiver
  Mod1 = Passive Buzzer

nets:
  GND: LED1.cathode, LED3.cathode, U1.GND, LED6.cathode, Arduino_Uno.GND, M1.GND, IR_Receiver1.GND, Mod1.-
  N1: LED1.anode, Arduino_Uno.D3_PWM
  N2: LED3.anode, Arduino_Uno.D2
  N3: U1.RXD, Arduino_Uno.A1
  VCC: U1.VCC, Arduino_Uno.3V3
  N4: U1.CH_PD, Arduino_Uno.A2
  N5: U1.TXD, Arduino_Uno.A0
  N6: LED6.anode, Arduino_Uno.D4
  N7: Arduino_Uno.D10_PWM/SS, IR_Receiver1.OUT
  N8: Arduino_Uno.D5_PWM, Mod1.S
  N9: Arduino_Uno.D6_PWM, M1.SIG
  VCC_2: Arduino_Uno.5V, M1.VCC, IR_Receiver1.VCC

custom parts:
  ESP8266 WiFi Module: Generic WiFi Module based on the ESP8266 with onboard PCB antenna and UART communications
  Grove Electromagnet: Grove Electromagnet.
  IR_Receiver: 赤外線受信モジュール GP1UXC41QS
