# Fritzing sketch SimonGame (saved by Fritzing 0.9.10b)
breadboards: 1

parts:
  LED1 = LED - 3mm [color="Red (633nm)" current=0.030 package="3 mm [THT]"]
  LED3 = LED - 3mm [color="Blue (470nm)" current=0.030 package="3 mm [THT]"]
  S2 = Momentary Switch [package=ksa_sealed_tac_switch]
  S3 = Momentary Switch [package=ksa_sealed_tac_switch]
  S4 = Momentary Switch [package=ksa_sealed_tac_switch]
  S5 = Momentary Switch [package=ksa_sealed_tac_switch]
  Mod1 = Passive Buzzer
  S1 = Momentary Switch [package=ksa_sealed_tac_switch]
  LED5 = LED - 3mm [color="Yellow (595nm)" current=0.030 package="3 mm [THT]"]
  U1 = ESP8266 WiFi Module [part_number=ESP8266]
  LED6 = LED - 3mm [color="Green (560nm)" current=0.030 package="3 mm [THT]"]
  Arduino_Uno = Arduino Uno (Rev3)
  U3 = FS1000A - 433Mhz RF Transmitter [package=THT]

nets:
  N1: LED1.cathode, Arduino_Uno.D6_PWM
  GND: LED1.anode, LED3.anode, S2.4, S3.4, S4.4, S5.4, Mod1.-, S1.4, LED5.anode, U1.GND, LED6.anode, Arduino_Uno.GND, U3.GND
  N2: LED3.cathode, Arduino_Uno.D4
  N3: S2.1, Arduino_Uno.D10_PWM/SS
  N4: S3.1, Arduino_Uno.D7
  N5: S4.1, Arduino_Uno.D8
  N6: S5.1, Arduino_Uno.D9_PWM
  N7: Mod1.S, Arduino_Uno.D2
  N8: S1.1, Arduino_Uno.D13/SCK
  N9: LED5.cathode, Arduino_Uno.D5_PWM
  N10: U1.RXD, Arduino_Uno.A1
  VCC: U1.VCC, Arduino_Uno.3V3
  N11: U1.CH_PD, Arduino_Uno.A2
  N12: U1.TXD, Arduino_Uno.A0
  N13: LED6.cathode, Arduino_Uno.D3_PWM
  N14: Arduino_Uno.A5/SCL, U3.DATA
  5V: Arduino_Uno.5V, U3.VCC

custom parts:
  ESP8266 WiFi Module: Generic WiFi Module based on the ESP8266 with onboard PCB antenna and UART communications
  FS1000A - 433Mhz RF Transmitter: This is 433Mhz RF transmitter with receiver kit for Arduino ARM MCU wireless Application environment: Remote control switch, receiver module, motorcycles, automobile anti-theft products, home security products, electric doors, shutter doors, windows, remote control socket, remote control LED, remote audio remote control electric doors, garage door remote control, remote control retractable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
