# Fritzing sketch SisDisplay (saved by Fritzing 0.9.10b)

parts:
  Composant1 = Arduino Uno (Rev3)  # not connected
  Composant2 = Base Shield V2
  U1 = ESP8266 WiFi Module [part_number=ESP8266]
  Grove3 = Grove OLED 128x96
  Grove_LED_Red1 = Grove LED Red
  Grove_Buzzer1 = Grove Buzzer

nets:
  N1: Composant2.D2, U1.TXD
  N2: Composant2.D3, U1.RXD
  N3: Composant2.D4, U1.CH_PD
  3V3: Composant2.3V3, U1.VCC
  GND: Composant2.GND, U1.GND
  N4: Composant2.pin_108, Grove_Buzzer1.GND
  N5: Composant2.pin_109, Grove_Buzzer1.VCC
  N6: Composant2.pin_110, Grove_Buzzer1.NC
  N7: Composant2.pin_111, Grove_Buzzer1.SIG
  N8: Composant2.pin_112, Grove_LED_Red1.GND
  N9: Composant2.pin_113, Grove_LED_Red1.NC2
  N10: Composant2.pin_114, Grove_LED_Red1.NC1
  N11: Composant2.pin_115, Grove_LED_Red1.SIG
  N12: Composant2.pin_128, Grove3.GND
  N13: Composant2.pin_129, Grove3.VCC
  N14: Composant2.pin_130, Grove3.SDA
  N15: Composant2.pin_131, Grove3.SCL

custom parts:
  ESP8266 WiFi Module: Generic WiFi Module based on the ESP8266 with onboard PCB antenna and UART communications
  Grove LED Red: LED red, Grove connector.
  Grove Buzzer: Buzzer, Grove connector.
