# Fritzing sketch SisSensor (saved by Fritzing 0.9.10b)

parts:
  Composant1 = Arduino Uno (Rev3)  # not connected
  Composant2 = Base Shield V2
  Grove1 = Grove 3 Axis Digital Accelerometer 16g
  U1 = ESP8266 WiFi Module [part_number=ESP8266]

nets:
  N1: Composant2.D2, U1.TXD
  N2: Composant2.D3, U1.RXD
  N3: Composant2.D4, U1.CH_PD
  3V3: Composant2.3V3, U1.VCC
  GND: Composant2.GND, U1.GND
  N4: Composant2.pin_136, Grove1.GND
  N5: Composant2.pin_137, Grove1.VCC
  N6: Composant2.pin_138, Grove1.SDA
  N7: Composant2.pin_139, Grove1.SCL

custom parts:
  ESP8266 WiFi Module: Generic WiFi Module based on the ESP8266 with onboard PCB antenna and UART communications
